# Fritzing sketch Cncv1 (saved by Fritzing 0.9.4)

parts:
  A1 = DM860A Stepper Motor Driver
  M1 = Stepper Motor - Unipolar  # not connected
  S1 = D2F-FL Omron Snap Action Limit Switch with Level
  S2 = Round Pushbutton
  Part1 = Arduino Uno (Rev3) - ICSP
  S3 = D2F-FL Omron Snap Action Limit Switch with Level

nets:
  N1: A1.ENBL-(ENB), Part1.D2
  N2: A1.ENBL+(+5V), A1.DIR+(+5V), A1.PUL+(+5V), Part1.5V
  N3: A1.DIR-(DIR), Part1.D3_PWM
  N4: A1.PUL-(PUL), Part1.D4
  N5: S1.Pin_1, S2.leg1, Part1.GND, S3.Pin_1
  N6: S1.Pin_2, Part1.D5_PWM
  N7: S2.leg0, Part1.A0
  N8: Part1.D6_PWM, S3.Pin_2

custom parts:
  DM860A Stepper Motor Driver: DM860A is a type of two-phase hybrid stepping motor driver, The drive voltage of which is from 24VDC to 80VDC. It is designed for use with 2-phase hybrid stepper motor of all kinds with 57mm to 110mm outside diameter and less than 8.0A phase current. Mar 2023: Correct pcb layerId as the part won't save correctly in a .fzz file as is.
  D2F-FL Omron Snap Action Limit Switch with Level: Snap action switch with stainless steel lever.
