# Fritzing sketch par_mem_load (saved by Fritzing 0.9.4)

parts:
  Part1 = Arduino Uno (Rev3) - ICSP
  microSD1 = MicroSD Card Module
  M1 = MAX485 Breakout [package=THT]
  U1 = Voltage Regulator - 5V [package="TO220 [THT]"]
  A1 = Apogee sp-110-ss [package=THT]
  Load_Cell2 = Load Cell - Red/white/black/green
  Part2 = HX711 Weighing Sensor Module
  S1 = Square Pushbutton

nets:
  N1: Part1.A0, Part2.DO/RX
  N2: Part1.A1, Part2.CK/TX
  N3: Part1.A2, S1.leg1
  N4: Part1.ICSP_MOSI, Part1.D11_PWM/MOSI, microSD1.MOSI
  N5: Part1.D8, M1.RE
  N6: Part1.D12/MISO, microSD1.MISO
  N7: Part1.D13/SCK, microSD1.SCK
  N8: Part1.D2, M1.RO
  N9: Part1.D3_PWM, M1.DI
  N10: Part1.D4, microSD1.CS
  N11: Part1.D7, M1.DE
  VCC: Part1.5V, microSD1.VCC, M1.VCC, U1.output_voltage, Part2.VCC
  GND: Part1.GND, microSD1.GND, M1.GND, U1.GND, A1.pin2, A1.pin3, Part2.GND, S1.leg0
  N12: U1.input_voltage, A1.pin1
  N13: Load_Cell2.wire1, Part2.E+
  N14: Load_Cell2.wire2, Part2.A+
  N15: Load_Cell2.wire3, Part2.E-
  N16: Load_Cell2.wire4, Part2.A-

notes:
  +12V Gnd

custom parts:
  MicroSD Card Module: A common microSD card module.
  MAX485 Breakout: MAX485 RS485 breakout board
  Apogee sp-110-ss: The SP-110 is a self-powered, analog sensor with a 0 to 400 mV output. The sensor incorporates a silicon-cell photodiode with a rugged, self-cleaning sensor housing design, and high-quality cable.
  Load Cell - Red/white/black/green: A rectangle load cell/weighting pressure Sensor with four wires - Red, white, black, green. Normally corresponding with E+, E-, A+, A- respectively.
  HX711 Weighing Sensor Module: HX711 is a precision 24-bit analog-to-digital converter (ADC) designed for weigh scales and industrial control applications to interface directly with a bridge sensor.
